// Logisim project 8BitComputer_OREN_PALEI_FINAL.circ as structural Verilog: 6 circuits, main circuit Memory_Cell
// OE TESTING DATA
module main (
  input  [7:0] testing_data,
  input  OE,
  input  Counter_oe,
  input  OE_TESTING_DATA,
  input  WE,
  input  [3:0] OE_TESTING,
  input  Count_Enable,
  input  WE_2,
  input  OE_2,
  input  OE_3,
  input  INTERNAL_OE,
  input  WE_3,
  input  OE_4,
  input  WE_4,
  input  OE_5,
  input  WE_5,
  input  WE_6,
  input  OE_6,
  input  OE_7,
  input  WE_7,
  output [3:0] MAR_CONTENT,
  output [3:0] out_22,
  output [7:0] instruction_register_CONTENT,
  output [7:0] MBR_CONTENT,
  output [7:0] REG_B_CONTENT,
  output [7:0] Stored_Data,
  output [7:0] ALU_RESULT,
  output [7:0] REG_B_CONTENT_2
);

  wire clock_1_out;
  wire [3:0] controlled_buffer_1_out, MAR_dout;
  wire [7:0] ALU_dout, bit_extender_1_out, Instruction_Register_dout;
  wire [15:0] DECIMAL_DECODER_4_out_2, DECIMAL_DECODER_4_out_2_2;
  wire [31:0] DECIMAL_DECODER_2_out_2, DECIMAL_DECODER_3_out_2, DECIMAL_DECODER_out_2;

  Counter #(.width(4), .max('h3)) counter_1 (
    .D(controlled_buffer_1_out), .count(Count_Enable), .Q(out_22), .clk(clock_1_out));  // open: load, carry, clr
  Clock clock_1 (.out(clock_1_out));
  assign controlled_buffer_1_out = Counter_oe ? out_22 : 4'bz;  // Controlled_Buffer controlled_buffer_1
  Register Instruction_Register (
    .Clock(clock_1_out), .WE(WE_3), .DIN(ALU_dout), .OE(OE_4), .Dout(Instruction_Register_dout),
    .Stored_Data(instruction_register_CONTENT));
  decimal_decoder DECIMAL_DECODER (.in_1(REG_B_CONTENT), .out_2(DECIMAL_DECODER_out_2));
  Register REGISTER_A (.Clock(clock_1_out), .WE(WE_5), .DIN(ALU_dout), .Stored_Data(REG_B_CONTENT));  // open: OE, Dout
  Register REGISTER_B (
    .Clock(clock_1_out), .WE(WE_7), .DIN(ALU_dout), .Stored_Data(REG_B_CONTENT_2));  // open: OE, Dout
  decimal_decoder DECIMAL_DECODER_2 (.in_1(REG_B_CONTENT_2), .out_2(DECIMAL_DECODER_2_out_2));
  BitSelector #(.group(4)) bitselector_1 (.in(Instruction_Register_dout), .out(controlled_buffer_1_out), .sel(1'b0));
  assign bit_extender_1_out = {{4{1'b0}}, out_22};  // Bit_Extender bit_extender_1
  _7_Segment_Display u_7_segment_display_1 (
    .g(DECIMAL_DECODER_out_2[15]), .f(DECIMAL_DECODER_out_2[14]), .a(DECIMAL_DECODER_out_2[13]),
    .b(DECIMAL_DECODER_out_2[12]), .e(DECIMAL_DECODER_out_2[31]), .d(DECIMAL_DECODER_out_2[30]),
    .c(DECIMAL_DECODER_out_2[29]), .dp(DECIMAL_DECODER_out_2[28]));
  ALU ALU (
    .REG_A(REG_B_CONTENT), .REG_B(REG_B_CONTENT_2), .OE(OE_7), .Dout(ALU_dout), .ALU_RES(ALU_RESULT));  // open: Carry_out
  _7_Segment_Display u_7_segment_display_2 (
    .g(DECIMAL_DECODER_2_out_2[15]), .f(DECIMAL_DECODER_2_out_2[14]), .a(DECIMAL_DECODER_2_out_2[13]),
    .b(DECIMAL_DECODER_2_out_2[12]), .e(DECIMAL_DECODER_2_out_2[31]), .d(DECIMAL_DECODER_2_out_2[30]),
    .c(DECIMAL_DECODER_2_out_2[29]), .dp(DECIMAL_DECODER_2_out_2[28]));
  _7_Segment_Display u_7_segment_display_3 (
    .g(DECIMAL_DECODER_2_out_2[11]), .f(DECIMAL_DECODER_2_out_2[10]), .a(DECIMAL_DECODER_2_out_2[9]),
    .b(DECIMAL_DECODER_2_out_2[8]), .e(DECIMAL_DECODER_2_out_2[27]), .d(DECIMAL_DECODER_2_out_2[26]),
    .c(DECIMAL_DECODER_2_out_2[25]), .dp(DECIMAL_DECODER_2_out_2[24]));
  _7_Segment_Display u_7_segment_display_4 (
    .g(DECIMAL_DECODER_3_out_2[3]), .f(DECIMAL_DECODER_3_out_2[2]), .a(DECIMAL_DECODER_3_out_2[1]),
    .b(DECIMAL_DECODER_3_out_2[0]), .e(DECIMAL_DECODER_3_out_2[19]), .d(DECIMAL_DECODER_3_out_2[18]),
    .c(DECIMAL_DECODER_3_out_2[17]), .dp(DECIMAL_DECODER_3_out_2[16]));
  decimal_decoder DECIMAL_DECODER_3 (.in_1(bit_extender_1_out), .out_2(DECIMAL_DECODER_3_out_2));
  _7_Segment_Display u_7_segment_display_5 (
    .g(DECIMAL_DECODER_out_2[7]), .f(DECIMAL_DECODER_out_2[6]), .a(DECIMAL_DECODER_out_2[5]),
    .b(DECIMAL_DECODER_out_2[4]), .e(DECIMAL_DECODER_out_2[23]), .d(DECIMAL_DECODER_out_2[22]),
    .c(DECIMAL_DECODER_out_2[21]), .dp(DECIMAL_DECODER_out_2[20]));
  _7_Segment_Display u_7_segment_display_6 (
    .g(DECIMAL_DECODER_out_2[11]), .f(DECIMAL_DECODER_out_2[10]), .a(DECIMAL_DECODER_out_2[9]),
    .b(DECIMAL_DECODER_out_2[8]), .e(DECIMAL_DECODER_out_2[27]), .d(DECIMAL_DECODER_out_2[26]),
    .c(DECIMAL_DECODER_out_2[25]), .dp(DECIMAL_DECODER_out_2[24]));
  _7_Segment_Display u_7_segment_display_7 (
    .g(DECIMAL_DECODER_2_out_2[3]), .f(DECIMAL_DECODER_2_out_2[2]), .a(DECIMAL_DECODER_2_out_2[1]),
    .b(DECIMAL_DECODER_2_out_2[0]), .e(DECIMAL_DECODER_2_out_2[19]), .d(DECIMAL_DECODER_2_out_2[18]),
    .c(DECIMAL_DECODER_2_out_2[17]), .dp(DECIMAL_DECODER_2_out_2[16]));
  _7_Segment_Display u_7_segment_display_8 (
    .g(DECIMAL_DECODER_2_out_2[7]), .f(DECIMAL_DECODER_2_out_2[6]), .a(DECIMAL_DECODER_2_out_2[5]),
    .b(DECIMAL_DECODER_2_out_2[4]), .e(DECIMAL_DECODER_2_out_2[23]), .d(DECIMAL_DECODER_2_out_2[22]),
    .c(DECIMAL_DECODER_2_out_2[21]), .dp(DECIMAL_DECODER_2_out_2[20]));
  _7_Segment_Display u_7_segment_display_9 (
    .g(DECIMAL_DECODER_out_2[3]), .f(DECIMAL_DECODER_out_2[2]), .a(DECIMAL_DECODER_out_2[1]),
    .b(DECIMAL_DECODER_out_2[0]), .e(DECIMAL_DECODER_out_2[19]), .d(DECIMAL_DECODER_out_2[18]),
    .c(DECIMAL_DECODER_out_2[17]), .dp(DECIMAL_DECODER_out_2[16]));
  LED D7 (.in(ALU_dout[7]));
  LED D6 (.in(ALU_dout[6]));
  assign ALU_dout = OE_TESTING_DATA ? testing_data : 8'bz;  // Controlled_Buffer controlled_buffer_2
  LED D5 (.in(ALU_dout[5]));
  LED D4 (.in(ALU_dout[4]));
  LED D2 (.in(ALU_dout[2]));
  LED D1 (.in(ALU_dout[1]));
  LED D3 (.in(ALU_dout[3]));
  LED D0 (.in(ALU_dout[0]));
  assign ALU_dout = INTERNAL_OE ? MBR_CONTENT : 8'bz;  // Controlled_Buffer controlled_buffer_3
  Register Output_Register (
    .Clock(clock_1_out), .WE(WE_6), .DIN(ALU_dout), .OE(OE_6), .Dout(ALU_dout), .Stored_Data(Stored_Data));
  Memory_Address_Register MAR (
    .Clock(clock_1_out), .WE(WE), .DIN(controlled_buffer_1_out), .OE(OE_3), .Dout(MAR_dout),
    .Stored_Data(MAR_CONTENT));
  Register register_1 (
    .Clock(clock_1_out), .WE(WE_4), .DIN(ALU_dout), .OE(OE_5), .Dout(ALU_dout), .Stored_Data(MBR_CONTENT));
  decimal_decoder DECIMAL_DECODER_4 (.in_1(Stored_Data), .out_2({DECIMAL_DECODER_4_out_2_2, DECIMAL_DECODER_4_out_2}));
  assign MAR_dout = OE ? OE_TESTING : 4'bz;  // Controlled_Buffer controlled_buffer_4
  _7_Segment_Display u_7_segment_display_10 (
    .g(DECIMAL_DECODER_4_out_2[15]), .f(DECIMAL_DECODER_4_out_2[14]), .a(DECIMAL_DECODER_4_out_2[13]),
    .b(DECIMAL_DECODER_4_out_2[12]), .e(DECIMAL_DECODER_4_out_2_2[15]), .d(DECIMAL_DECODER_4_out_2_2[14]),
    .c(DECIMAL_DECODER_4_out_2_2[13]), .dp(DECIMAL_DECODER_4_out_2_2[12]));
  _7_Segment_Display u_7_segment_display_11 (
    .g(DECIMAL_DECODER_4_out_2[11]), .f(DECIMAL_DECODER_4_out_2[10]), .a(DECIMAL_DECODER_4_out_2[9]),
    .b(DECIMAL_DECODER_4_out_2[8]), .e(DECIMAL_DECODER_4_out_2_2[11]), .d(DECIMAL_DECODER_4_out_2_2[10]),
    .c(DECIMAL_DECODER_4_out_2_2[9]), .dp(DECIMAL_DECODER_4_out_2_2[8]));
  _7_Segment_Display u_7_segment_display_12 (
    .g(DECIMAL_DECODER_4_out_2[7]), .f(DECIMAL_DECODER_4_out_2[6]), .a(DECIMAL_DECODER_4_out_2[5]),
    .b(DECIMAL_DECODER_4_out_2[4]), .e(DECIMAL_DECODER_4_out_2_2[7]), .d(DECIMAL_DECODER_4_out_2_2[6]),
    .c(DECIMAL_DECODER_4_out_2_2[5]), .dp(DECIMAL_DECODER_4_out_2_2[4]));
  _7_Segment_Display u_7_segment_display_13 (
    .g(DECIMAL_DECODER_4_out_2[3]), .f(DECIMAL_DECODER_4_out_2[2]), .a(DECIMAL_DECODER_4_out_2[1]),
    .b(DECIMAL_DECODER_4_out_2[0]), .e(DECIMAL_DECODER_4_out_2_2[3]), .d(DECIMAL_DECODER_4_out_2_2[2]),
    .c(DECIMAL_DECODER_4_out_2_2[1]), .dp(DECIMAL_DECODER_4_out_2_2[0]));
  LED D4_2 (.in(ALU_dout[4]));
  LED D7_2 (.in(ALU_dout[7]));
  LED D6_2 (.in(ALU_dout[6]));
  LED D5_2 (.in(ALU_dout[5]));
  LED D3_2 (.in(ALU_dout[3]));
  LED D2_2 (.in(ALU_dout[2]));
  LED D0_2 (.in(ALU_dout[0]));
  LED D1_2 (.in(ALU_dout[1]));
  RAM #(.addrWidth(4), .bus("separate")) ram_1 (
    .addr(MAR_dout), .din(ALU_dout), .data(ALU_dout), .str(WE_2), .clk(clock_1_out), .ld(OE_2));  // open: sel, clr

  // Notes on the sheet:
  //   PC
  //   internal address bus(4 bits)
  //   internal data bus
  //   MBR
  //   external address bus
  //   EXTERNAL DATA BUS
endmodule

module Memory_Cell (
  input  Clock,
  input  WE,
  input  DIN,
  input  OE,
  input  RESET,
  output Dout,
  output Stored_data
);

  wire and_1_out, and_2_out, not_1_out, or_1_out;

  not not_1 (not_1_out, WE);
  and and_1 (and_1_out, Stored_data, not_1_out);
  and and_2 (and_2_out, WE, DIN);
  or or_1 (or_1_out, and_1_out, and_2_out);
  D_Flip_Flop d_ff_1 (.clk(Clock), .D(or_1_out), .Q(Stored_data), .reset(RESET));  // open: Qn, preset, en
  assign Dout = OE ? Stored_data : 1'bz;  // Controlled_Buffer controlled_buffer_1
endmodule

module Register (
  input  Clock,
  input  WE,
  input  [7:0] DIN,
  input  OE,
  output [7:0] Dout,
  output [7:0] Stored_Data
);

  Memory_Cell _0 (
    .Clock(Clock), .WE(WE), .DIN(DIN[0]), .OE(OE), .Dout(Dout[0]), .Stored_data(Stored_Data[0]));  // open: RESET
  Memory_Cell _1 (
    .Clock(Clock), .WE(WE), .DIN(DIN[1]), .OE(OE), .Dout(Dout[1]), .Stored_data(Stored_Data[1]));  // open: RESET
  Memory_Cell _2 (
    .Clock(Clock), .WE(WE), .DIN(DIN[2]), .OE(OE), .Dout(Dout[2]), .Stored_data(Stored_Data[2]));  // open: RESET
  Memory_Cell _3 (
    .Clock(Clock), .WE(WE), .DIN(DIN[3]), .OE(OE), .Dout(Dout[3]), .Stored_data(Stored_Data[3]));  // open: RESET
  Memory_Cell _4 (
    .Clock(Clock), .WE(WE), .DIN(DIN[4]), .OE(OE), .Dout(Dout[4]), .Stored_data(Stored_Data[4]));  // open: RESET
  Memory_Cell _5 (
    .Clock(Clock), .WE(WE), .DIN(DIN[5]), .OE(OE), .Dout(Dout[5]), .Stored_data(Stored_Data[5]));  // open: RESET
  Memory_Cell _6 (
    .Clock(Clock), .WE(WE), .DIN(DIN[6]), .OE(OE), .Dout(Dout[6]), .Stored_data(Stored_Data[6]));  // open: RESET
  Memory_Cell _7 (
    .Clock(Clock), .WE(WE), .DIN(DIN[7]), .OE(OE), .Dout(Dout[7]), .Stored_data(Stored_Data[7]));  // open: RESET

  // Notes on the sheet:
  //   Register 8 bits
endmodule

module Memory_Address_Register (
  input  Clock,
  input  WE,
  input  [3:0] DIN,
  input  OE,
  output [3:0] Dout,
  output [3:0] Stored_Data
);

  Memory_Cell _0 (
    .Clock(Clock), .WE(WE), .DIN(DIN[0]), .OE(OE), .Dout(Dout[0]), .Stored_data(Stored_Data[0]));  // open: RESET
  Memory_Cell _1 (
    .Clock(Clock), .WE(WE), .DIN(DIN[1]), .OE(OE), .Dout(Dout[1]), .Stored_data(Stored_Data[1]));  // open: RESET
  Memory_Cell _2 (
    .Clock(Clock), .WE(WE), .DIN(DIN[2]), .OE(OE), .Dout(Dout[2]), .Stored_data(Stored_Data[2]));  // open: RESET
  Memory_Cell _3 (
    .Clock(Clock), .WE(WE), .DIN(DIN[3]), .OE(OE), .Dout(Dout[3]), .Stored_data(Stored_Data[3]));  // open: RESET

  // Notes on the sheet:
  //   MAR
endmodule

module ALU (
  input  [7:0] REG_A,
  input  [7:0] REG_B,
  input  OE,
  output [7:0] Dout,
  output [7:0] ALU_RES,
  output Carry_out
);

  Adder adder_1 (.a(REG_A), .b(REG_B), .out(ALU_RES), .cout(Carry_out));  // open: cin
  assign Dout = OE ? ALU_RES : 8'bz;  // Controlled_Buffer controlled_buffer_1

  // Notes on the sheet:
  //   ALU 8 BITS
endmodule

module decimal_decoder (
  input  [7:0] in_1,
  output [31:0] out_2
);

  ROM #(.dataWidth(32)) rom_1 (
    .addr(in_1),
    .data({out_2[31:28], out_2[15:12], out_2[27:24], out_2[11:8], out_2[23:20], out_2[7:4], out_2[19:16], out_2[3:0]}));  // open: sel

  // Notes on the sheet:
  //   DIN
  //   contents of rom_1 (hex, n*v repeats v):
  //   e7 21 cb 6b 2d 6e ee 23 ef 2f 21e7 2121 21cb 216b 212d 216e 21ee 2123 21ef 212f cbe7 cb21 cbcb cb6b
  //   cb2d cb6e cbee cb23 cbef cb2f 6be7 6b21 6bcb 6b6b 6b2d 6b6e 6bee 6b23 6bef 6b2f 2de7 2d21 2dcb 2d6b
  //   2d2d 2d6e 2dee 2d23 2def 2d2f 6ee7 6e21 6ecb 6e6b 6e2d 6e6e 6eee 6e23 6eef 6e2f eee7 ee21 eecb ee6b
  //   ee2d ee6e eeee ee23 eeef ee2f 23e7 2321 23cb 236b 232d 236e 23ee 2323 23ef 232f efe7 ef21 efcb ef6b
  //   ef2d ef6e efee ef23 efef ef2f 2fe7 2f21 2fcb 2f6b 2f2d 2f6e 2fee 2f23 2fef 2f2f 21e7e7 21e721 21e7cb
  //   21e76b 21e72d 21e76e 21e7ee 21e723 21e7ef 21e72f 2121e7 212121 2121cb 21216b 21212d 21216e 2121ee
  //   212123 2121ef 21212f 21cbe7 21cb21 21cbcb 21cb6b 21cb2d 21cb6e 21cbee 21cb23 21cbef 21cb2f 216be7
  //   216b21 216bcb 216b6b 216b2d 216b6e 216bee 216b23 216bef 216b2f 212de7 212d21 212dcb 212d6b 212d2d
  //   212d6e 212dee 212d23 212def 212d2f 216ee7 216e21 216ecb 216e6b 216e2d 216e6e 216eee 216e23 216eef
  //   216e2f 21eee7 21ee21 21eecb 21ee6b 21ee2d 21ee6e 21eeee 21ee23 21eeef 21ee2f 2123e7 212321 2123cb
  //   21236b 21232d 21236e 2123ee 212323 2123ef 21232f 21efe7 21ef21 21efcb 21ef6b 21ef2d 21ef6e 21efee
  //   21ef23 21efef 21ef2f 212fe7 212f21 212fcb 212f6b 212f2d 212f6e 212fee 212f23 212fef 212f2f cbe7e7
  //   cbe721 cbe7cb cbe76b cbe72d cbe76e cbe7ee cbe723 cbe7ef cbe72f cb21e7 cb2121 cb21cb cb216b cb212d
  //   cb216e cb21ee cb2123 cb21ef cb212f cbcbe7 cbcb21 cbcbcb cbcb6b cbcb2d cbcb6e cbcbee cbcb23 cbcbef
  //   cbcb2f cb6be7 cb6b21 cb6bcb cb6b6b cb6b2d cb6b6e cb6bee cb6b23 cb6bef cb6b2f cb2de7 cb2d21 cb2dcb
  //   cb2d6b cb2d2d cb2d6e cb2dee cb2d23 cb2def cb2d2f cb6ee7 cb6e21 cb6ecb cb6e6b cb6e2d cb6e6e
  //   decimal decoder
endmodule
