// Logisim project CPU_FINAL.circ as structural Verilog: 5 circuits, main circuit main
module main (
  input  [7:0] testing_data,
  input  Counter_oe,
  input  OE_TESTING_DATA,
  input  WE,
  input  Count_Enable,
  input  OE,
  input  INTERNAL_OE,
  input  WE_2,
  input  OE_2,
  input  WE_3,
  input  OE_3,
  input  WE_4,
  input  OE_4,
  input  WE_5,
  input  OE_5,
  input  OE_6,
  input  WE_6,
  input  OE_7,
  output [3:0] MAR_CONTENT,
  output [3:0] out_20,
  output [7:0] instruction_register_CONTENT,
  output [7:0] MBR_CONTENT,
  output [7:0] REG_A_CONTENT,
  output [7:0] Stored_Data,
  output [7:0] ALU_RESULT,
  output [7:0] REG_B_CONTENT
);

  wire clock_1_out;
  wire [3:0] controlled_buffer_1_out, MAR_dout;
  wire [7:0] ALU_dout, Instruction_Register_dout;

  Counter #(.width(4), .max('h3)) counter_1 (
    .D(controlled_buffer_1_out), .count(Count_Enable), .Q(out_20), .clk(clock_1_out));  // open: load, carry, clr
  Clock clock_1 (.out(clock_1_out));
  assign controlled_buffer_1_out = Counter_oe ? out_20 : 4'bz;  // Controlled_Buffer controlled_buffer_1
  Register Instruction_Register (
    .Clock(clock_1_out), .WE(WE_2), .DIN(ALU_dout), .OE(OE_2), .Dout(Instruction_Register_dout),
    .Stored_Data(instruction_register_CONTENT));
  Register REGISTER_A (
    .Clock(clock_1_out), .WE(WE_4), .DIN(ALU_dout), .OE(OE_4), .Stored_Data(REG_A_CONTENT));  // open: Dout
  Register B (.Clock(clock_1_out), .WE(WE_6), .DIN(ALU_dout), .OE(OE_7), .Stored_Data(REG_A_CONTENT));  // open: Dout
  BitSelector #(.group(4)) bitselector_1 (.in(Instruction_Register_dout), .out(controlled_buffer_1_out), .sel(1'b0));
  ALU ALU (
    .REG_A(REG_A_CONTENT), .REG_B(REG_A_CONTENT), .OE(OE_6), .Dout(ALU_dout), .ALU_RES(ALU_RESULT));  // open: Carry_out
  LED D6 (.in(ALU_dout[6]));
  LED D7 (.in(ALU_dout[7]));
  assign ALU_dout = OE_TESTING_DATA ? testing_data : 8'bz;  // Controlled_Buffer controlled_buffer_2
  LED D5 (.in(ALU_dout[5]));
  LED D4 (.in(ALU_dout[4]));
  LED D2 (.in(ALU_dout[2]));
  LED D3 (.in(ALU_dout[3]));
  LED D1 (.in(ALU_dout[1]));
  LED D0 (.in(ALU_dout[0]));
  assign ALU_dout = INTERNAL_OE ? MBR_CONTENT : 8'bz;  // Controlled_Buffer controlled_buffer_3
  Register Output_Register (
    .Clock(clock_1_out), .WE(WE_5), .DIN(ALU_dout), .OE(OE_5), .Dout(ALU_dout), .Stored_Data(Stored_Data));
  Memory_Address_Register MAR (
    .Clock(clock_1_out), .WE(WE), .DIN(controlled_buffer_1_out), .OE(OE), .Dout(MAR_dout),
    .Stored_Data(MAR_CONTENT));
  Register register_1 (
    .Clock(clock_1_out), .WE(WE_3), .DIN(ALU_dout), .OE(OE_3), .Dout(ALU_dout), .Stored_Data(MBR_CONTENT));
  LED D4_2 (.in(ALU_dout[4]));
  LED D7_2 (.in(ALU_dout[7]));
  LED D6_2 (.in(ALU_dout[6]));
  LED D5_2 (.in(ALU_dout[5]));
  LED D3_2 (.in(ALU_dout[3]));
  LED D0_2 (.in(ALU_dout[0]));
  LED D2_2 (.in(ALU_dout[2]));
  LED D1_2 (.in(ALU_dout[1]));

  assign REG_B_CONTENT = REG_A_CONTENT;

  // Notes on the sheet:
  //   PC
  //   internal address bus(4 bits)
  //   internal data bus
  //   MBR
  //   external address bus
  //   EXTERNAL DATA BUS
endmodule

module Memory_Cell (
  input  Clock,
  input  WE,
  input  DIN,
  input  OE,
  input  RESET,
  output Dout,
  output Stored_data
);

  wire and_1_out, and_2_out, not_1_out, or_1_out;

  not not_1 (not_1_out, WE);
  and and_1 (and_1_out, Stored_data, not_1_out);
  and and_2 (and_2_out, WE, DIN);
  or or_1 (or_1_out, and_1_out, and_2_out);
  D_Flip_Flop d_ff_1 (.clk(Clock), .D(or_1_out), .Q(Stored_data), .reset(RESET));  // open: Qn, preset, en
  assign Dout = OE ? Stored_data : 1'bz;  // Controlled_Buffer controlled_buffer_1
endmodule

module Register (
  input  Clock,
  input  WE,
  input  [7:0] DIN,
  input  OE,
  output [7:0] Dout,
  output [7:0] Stored_Data
);

  Memory_Cell _0 (
    .Clock(Clock), .WE(WE), .DIN(DIN[0]), .OE(OE), .Dout(Dout[0]), .Stored_data(Stored_Data[0]));  // open: RESET
  Memory_Cell _1 (
    .Clock(Clock), .WE(WE), .DIN(DIN[1]), .OE(OE), .Dout(Dout[1]), .Stored_data(Stored_Data[1]));  // open: RESET
  Memory_Cell _2 (
    .Clock(Clock), .WE(WE), .DIN(DIN[2]), .OE(OE), .Dout(Dout[2]), .Stored_data(Stored_Data[2]));  // open: RESET
  Memory_Cell _3 (
    .Clock(Clock), .WE(WE), .DIN(DIN[3]), .OE(OE), .Dout(Dout[3]), .Stored_data(Stored_Data[3]));  // open: RESET
  Memory_Cell _4 (
    .Clock(Clock), .WE(WE), .DIN(DIN[4]), .OE(OE), .Dout(Dout[4]), .Stored_data(Stored_Data[4]));  // open: RESET
  Memory_Cell _5 (
    .Clock(Clock), .WE(WE), .DIN(DIN[5]), .OE(OE), .Dout(Dout[5]), .Stored_data(Stored_Data[5]));  // open: RESET
  Memory_Cell _6 (
    .Clock(Clock), .WE(WE), .DIN(DIN[6]), .OE(OE), .Dout(Dout[6]), .Stored_data(Stored_Data[6]));  // open: RESET
  Memory_Cell _7 (
    .Clock(Clock), .WE(WE), .DIN(DIN[7]), .OE(OE), .Dout(Dout[7]), .Stored_data(Stored_Data[7]));  // open: RESET

  // Notes on the sheet:
  //   Register 8 bits
endmodule

module ALU (
  input  [7:0] REG_A,
  input  [7:0] REG_B,
  input  OE,
  output [7:0] Dout,
  output [7:0] ALU_RES,
  output Carry_out
);

  Adder adder_1 (.a(REG_A), .b(REG_B), .out(ALU_RES), .cout(Carry_out));  // open: cin
  assign Dout = OE ? ALU_RES : 8'bz;  // Controlled_Buffer controlled_buffer_1

  // Notes on the sheet:
  //   ALU 8 BITS
endmodule

module Memory_Address_Register (
  input  Clock,
  input  WE,
  input  [3:0] DIN,
  input  OE,
  output [3:0] Dout,
  output [3:0] Stored_Data
);

  Memory_Cell _0 (
    .Clock(Clock), .WE(WE), .DIN(DIN[0]), .OE(OE), .Dout(Dout[0]), .Stored_data(Stored_Data[0]));  // open: RESET
  Memory_Cell _1 (
    .Clock(Clock), .WE(WE), .DIN(DIN[1]), .OE(OE), .Dout(Dout[1]), .Stored_data(Stored_Data[1]));  // open: RESET
  Memory_Cell _2 (
    .Clock(Clock), .WE(WE), .DIN(DIN[2]), .OE(OE), .Dout(Dout[2]), .Stored_data(Stored_Data[2]));  // open: RESET
  Memory_Cell _3 (
    .Clock(Clock), .WE(WE), .DIN(DIN[3]), .OE(OE), .Dout(Dout[3]), .Stored_data(Stored_Data[3]));  // open: RESET

  // Notes on the sheet:
  //   MAR
endmodule
